# Fritzing sketch Untitled Sketch 2 (saved by Fritzing 0.9.3b)

parts:
  SIM800L_BO1 = SIM800L BO
  Part1 = Arduino Nano (Rev3.0)
  R1 = Resistor [tolerance=±5% resistance=10k package="0402 [SMD]"]
  R2 = Resistor [tolerance=±5% resistance=22k package="0402 [SMD]"]
  J2 = 2.1mm Barrel Jack with Terminal Block
  ANT1 = Antenna
  U2 = LIPO-110mAh [package=lipo-110]
  SP1 = SPEAKER [package=pcb_mount_speaker]
  Power_plug1 = Power plug
  Part2 = Jtron 1 Channel Optoisolated Relay Module [package=relay]

nets:
  N1: SIM800L_BO1.PIN1, ANT1.antenna_lead
  N2: SIM800L_BO1.PIN2, J2.POS, U2.+
  N3: SIM800L_BO1.pin_4, R1.Pin_1, R2.Pin_0
  N4: SIM800L_BO1.pin_5, Part1.D10
  N5: SIM800L_BO1.pin_6, R2.Pin_1, J2.NEG, U2.-
  GND: Part1.GND, Part2.GND
  N6: Part1.D2, Part2.IN1
  N7: Part1.D11/MOSI, R1.Pin_0
  N8: SP1.+, Power_plug1.VCC
  N9: SP1.-, Part2.NO
  N10: Power_plug1.GND, Part2.MAIN
