# Fritzing sketch Untitled Sketch 2 (saved by Fritzing 0.9.3b)

parts:
  SIM800L_BO1 = SIM800L BO
  Part1 = Arduino Nano (Rev3.0)
  T1 = LM35 Temperature Sensor [package="TO92 [THT]"]
  J1 = Piezo Speaker
  S1 = Square Pushbutton
  Part2 = MQ-4
  R1 = Resistor [tolerance=±5% resistance=10k package="0402 [SMD]"]
  R2 = Resistor [tolerance=±5% resistance=22k package="0402 [SMD]"]
  J2 = 2.1mm Barrel Jack with Terminal Block
  R4 = Resistor [tolerance=±5% resistance=20k package=THT]
  S2 = Round Pushbutton
  ANT1 = Antenna
  U2 = LIPO-110mAh [package=lipo-110]
  R3 = Resistor [tolerance=±5% resistance=20k package=THT]

nets:
  N1: SIM800L_BO1.PIN1, ANT1.antenna_lead
  N2: SIM800L_BO1.PIN2, J2.POS, R4.Pin_0, U2.+
  N3: SIM800L_BO1.pin_4, R1.Pin_1, R2.Pin_0
  N4: SIM800L_BO1.pin_5, Part1.D10
  N5: SIM800L_BO1.pin_6, J1.pin1, R2.Pin_1, J2.NEG, S2.leg0, U2.-
  GND: Part1.GND, T1.GND, S1.leg0, Part2.GND
  N6: Part1.D4, R4.Pin_1, S2.leg1
  N7: Part1.D6, J1.pin2
  N8: Part1.D11/MOSI, R1.Pin_0
  5V: Part1.5V, T1.+Vs, S1.leg1, Part2.VCC, R3.Pin_0
  N9: Part1.A2, R3.Pin_1
  N10: Part1.A1, T1.Vout
  N11: Part1.A0, Part2.AO
